# Fritzing sketch circuit (saved by Fritzing 0.9.3b)
breadboards: 1

parts:
  Raspberry_Pi_1 = Raspberry Pi 3 [part_number=RPI-3-V1.2]
  R1 = Resistor [tolerance=±5% resistance=220 package="2512 [SMD]"]
  LED2 = smd LED [color="Red (633nm)" package="0603 [SMD]"]
  LED3 = smd LED [color="Red (633nm)" package="0603 [SMD]"]
  S2 = Pushbutton [package="[SMD]"]

nets:
  N1: Raspberry_Pi_1.GPIO2, LED3.anode
  N2: Raspberry_Pi_1.GPIO3, LED2.anode
  N3: Raspberry_Pi_1.GIPO4, S2.Pin_3, S2.Pin_4
  N4: Raspberry_Pi_1.GND, R1.Pin_0, S2.Pin_1, S2.Pin_2
  N5: R1.Pin_1, LED2.cathode, LED3.cathode
